// Logisim project qtictactoe.circ as structural Verilog: 16 circuits, main circuit main
module main (
);

  wire CPU_MOV_out, engine_1_draw, engine_1_over, engine_1_p1_turn, engine_1_p1_won, engine_1_p2_turn,
       engine_1_p2_won, engine_1_start, PLR_1_MOV_out, PLR_2_MOV_out, RESET_out;
  wire [8:0] button_1_out, engine_1_board_p1, engine_1_board_p2, engine_1_mov_slct_state;

  Button button_1 (.out(button_1_out[0]));
  Button button_2 (.out(button_1_out[3]));
  Button button_3 (.out(button_1_out[6]));
  LED led_1 (.in(engine_1_mov_slct_state[0]));
  LED led_2 (.in(engine_1_mov_slct_state[3]));
  LED led_3 (.in(engine_1_mov_slct_state[6]));
  Button button_4 (.out(button_1_out[2]));
  Button button_5 (.out(button_1_out[1]));
  Button button_6 (.out(button_1_out[4]));
  Button button_7 (.out(button_1_out[5]));
  Button button_8 (.out(button_1_out[7]));
  Button button_9 (.out(button_1_out[8]));
  LED led_4 (.in(engine_1_mov_slct_state[1]));
  LED led_5 (.in(engine_1_mov_slct_state[4]));
  LED led_6 (.in(engine_1_mov_slct_state[7]));
  Button PLR_1_MOV (.out(PLR_1_MOV_out));
  Button PLR_2_MOV (.out(PLR_2_MOV_out));
  Button CPU_MOV (.out(CPU_MOV_out));
  Button RESET (.out(RESET_out));
  LED led_7 (.in(engine_1_mov_slct_state[2]));
  LED led_8 (.in(engine_1_mov_slct_state[5]));
  LED led_9 (.in(engine_1_mov_slct_state[8]));
  LED P1_TURN (.in(engine_1_p1_turn));
  LED P2_TURN (.in(engine_1_p2_turn));
  LED START (.in(engine_1_start));
  LED OVER (.in(engine_1_over));
  ENGINE engine_1 (
    .PLR_1_MOV(PLR_1_MOV_out), .PLR_2_MOV(PLR_2_MOV_out), .CPU_MOV(CPU_MOV_out), .RESET(RESET_out),
    .MOV_SLCT_INPUT(button_1_out), .MOV_SLCT_STATE(engine_1_mov_slct_state), .P1_TURN(engine_1_p1_turn),
    .P2_TURN(engine_1_p2_turn), .START(engine_1_start), .OVER(engine_1_over), .P1_WON(engine_1_p1_won),
    .P2_WON(engine_1_p2_won), .DRAW(engine_1_draw), .BOARD_P1(engine_1_board_p1), .BOARD_P2(engine_1_board_p2));
  LED P1_WON (.in(engine_1_p1_won));
  LED P2_WON (.in(engine_1_p2_won));
  LED DRAW (.in(engine_1_draw));
  LED led_10 (.in(engine_1_board_p1[0]));
  LED led_11 (.in(engine_1_board_p1[3]));
  LED led_12 (.in(engine_1_board_p1[6]));
  LED led_13 (.in(engine_1_board_p2[0]));
  LED led_14 (.in(engine_1_board_p2[3]));
  LED led_15 (.in(engine_1_board_p2[6]));
  LED led_16 (.in(engine_1_board_p2[1]));
  LED led_17 (.in(engine_1_board_p1[1]));
  LED led_18 (.in(engine_1_board_p2[4]));
  LED led_19 (.in(engine_1_board_p1[4]));
  LED led_20 (.in(engine_1_board_p1[7]));
  LED led_21 (.in(engine_1_board_p2[7]));
  LED led_22 (.in(engine_1_board_p2[2]));
  LED led_23 (.in(engine_1_board_p1[2]));
  LED led_24 (.in(engine_1_board_p1[5]));
  LED led_25 (.in(engine_1_board_p2[5]));
  LED led_26 (.in(engine_1_board_p2[8]));
  LED led_27 (.in(engine_1_board_p1[8]));
endmodule

module ENGINE (
  input  PLR_1_MOV,
  input  PLR_2_MOV,
  input  CPU_MOV,
  input  RESET,
  input  [8:0] MOV_SLCT_INPUT,
  output P1_TURN,
  output P2_TURN,
  output START,
  output OVER,
  output P1_WON,
  output P2_WON,
  output DRAW,
  output [8:0] BOARD_P1,
  output [8:0] BOARD_P2,
  output [8:0] MOV_SLCT_STATE
);

  wire and_1_out, and_2_out, and_3_out, not_1_out, p_mov_ok_1_mov_ok, state_machine_1_p1_turn,
       state_machine_1_p1_wrt, state_machine_1_p2_swtch, state_machine_1_p2_turn, state_machine_1_p2_wrt;
  wire [8:0] cpu_1_cpu, p2_switch_1_out;

  and and_1 (and_1_out, not_1_out, PLR_1_MOV);
  and and_2 (and_2_out, not_1_out, PLR_2_MOV);
  and and_3 (and_3_out, not_1_out, CPU_MOV);
  MOV_SELECT_MEM mov_select_mem_1 (.RESET(RESET), .INPUT(MOV_SLCT_INPUT), .OUTPUT(MOV_SLCT_STATE));
  and and_4 (P1_TURN, not_1_out, state_machine_1_p1_turn);
  and and_5 (P2_TURN, not_1_out, state_machine_1_p2_turn);
  STATE_MACHINE state_machine_1 (
    .P1(and_1_out), .P2(and_2_out), .CPU(and_3_out), .MOV_OK(p_mov_ok_1_mov_ok), .RESET(RESET),
    .P2_SWTCH(state_machine_1_p2_swtch), .P1_WRT(state_machine_1_p1_wrt), .P2_WRT(state_machine_1_p2_wrt),
    .P1_TURN(state_machine_1_p1_turn), .P2_TURN(state_machine_1_p2_turn), .START_TURN(START));
  not not_1 (not_1_out, OVER);
  P2_SWITCH p2_switch_1 (
    .PLR_MOV(MOV_SLCT_STATE), .CPU_MOV(cpu_1_cpu), .doPLR(state_machine_1_p2_swtch), .OUT(p2_switch_1_out));
  BOARD_MEM_1 board_mem_1_1 (.RESET(RESET), .WRT(state_machine_1_p1_wrt), .INP(MOV_SLCT_STATE), .STATE(BOARD_P1));
  BOARD_MEM_1 board_mem_1_2 (.RESET(RESET), .WRT(state_machine_1_p2_wrt), .INP(p2_switch_1_out), .STATE(BOARD_P2));
  END_DTCT end_dtct_1 (.P1(BOARD_P1), .P2(BOARD_P2), .P1_WIN(P1_WON), .P2_WIN(P2_WON), .DRAW(DRAW), .GAME_OVER(OVER));
  P_MOV_OK p_mov_ok_1 (.B1_state(BOARD_P1), .B2_state(BOARD_P2), .pmov(MOV_SLCT_STATE), .MOV_OK(p_mov_ok_1_mov_ok));
  CPU cpu_1 (.P1(BOARD_P1), .P2(BOARD_P2), .CPU(cpu_1_cpu));

  // Other names for the same wires on the sheet: ERST = RESET
endmodule

module MOV_SELECT_MEM (
  input  RESET,
  input  [8:0] INPUT,
  output [8:0] OUTPUT
);

  wire or_1_out, or_2_out, or_3_out, or_4_out, or_5_out, or_6_out, or_7_out, or_8_out, or_9_out;

  or or_1 (or_1_out, INPUT[1], INPUT[2], INPUT[3], INPUT[4], INPUT[5], INPUT[6], INPUT[7], INPUT[8], RESET);
  or or_2 (or_2_out, INPUT[0], INPUT[1], INPUT[2], INPUT[4], INPUT[5], INPUT[6], INPUT[7], INPUT[8], RESET);
  or or_3 (or_3_out, INPUT[0], INPUT[1], INPUT[2], INPUT[3], INPUT[4], INPUT[5], INPUT[7], INPUT[8], RESET);
  P_MOV_OK p_mov_ok_1 ();  // open: B1_state, B2_state, pmov, MOV_OK
  or or_4 (or_4_out, INPUT[0], INPUT[2], INPUT[3], INPUT[4], INPUT[5], INPUT[6], INPUT[7], INPUT[8], RESET);
  or or_5 (or_5_out, INPUT[0], INPUT[1], INPUT[2], INPUT[3], INPUT[5], INPUT[6], INPUT[7], INPUT[8], RESET);
  or or_6 (or_6_out, INPUT[0], INPUT[1], INPUT[2], INPUT[3], INPUT[4], INPUT[5], INPUT[6], INPUT[8], RESET);
  or or_7 (or_7_out, INPUT[0], INPUT[1], INPUT[3], INPUT[4], INPUT[5], INPUT[6], INPUT[7], INPUT[8], RESET);
  or or_8 (or_8_out, INPUT[0], INPUT[1], INPUT[2], INPUT[3], INPUT[4], INPUT[6], INPUT[7], INPUT[8], RESET);
  or or_9 (or_9_out, INPUT[0], INPUT[1], INPUT[2], INPUT[3], INPUT[4], INPUT[5], INPUT[6], INPUT[7], RESET);
  S_R_Flip_Flop #(.trigger("high")) s_r_ff_1 (
    .S(INPUT[0]), .clk(1'b1), .R(or_1_out), .Q(OUTPUT[0]));  // open: Qn, preset, reset, en
  S_R_Flip_Flop #(.trigger("high")) s_r_ff_2 (
    .S(INPUT[3]), .clk(1'b1), .R(or_2_out), .Q(OUTPUT[3]));  // open: Qn, preset, reset, en
  S_R_Flip_Flop #(.trigger("high")) s_r_ff_3 (
    .S(INPUT[6]), .clk(1'b1), .R(or_3_out), .Q(OUTPUT[6]));  // open: Qn, preset, reset, en
  S_R_Flip_Flop #(.trigger("high")) s_r_ff_4 (
    .S(INPUT[1]), .clk(1'b1), .R(or_4_out), .Q(OUTPUT[1]));  // open: Qn, preset, reset, en
  S_R_Flip_Flop #(.trigger("high")) s_r_ff_5 (
    .S(INPUT[4]), .clk(1'b1), .R(or_5_out), .Q(OUTPUT[4]));  // open: Qn, preset, reset, en
  S_R_Flip_Flop #(.trigger("high")) s_r_ff_6 (
    .S(INPUT[7]), .clk(1'b1), .R(or_6_out), .Q(OUTPUT[7]));  // open: Qn, preset, reset, en
  S_R_Flip_Flop #(.trigger("high")) s_r_ff_7 (
    .S(INPUT[2]), .clk(1'b1), .R(or_7_out), .Q(OUTPUT[2]));  // open: Qn, preset, reset, en
  S_R_Flip_Flop #(.trigger("high")) s_r_ff_8 (
    .S(INPUT[5]), .clk(1'b1), .R(or_8_out), .Q(OUTPUT[5]));  // open: Qn, preset, reset, en
  S_R_Flip_Flop #(.trigger("high")) s_r_ff_9 (
    .S(INPUT[8]), .clk(1'b1), .R(or_9_out), .Q(OUTPUT[8]));  // open: Qn, preset, reset, en

  // Other names for the same wires on the sheet: MOVSEL_0 = INPUT[0]; MOVSEL_1 = INPUT[1]; MOVSEL_2 = INPUT[2];
  //   MOVSEL_3 = INPUT[3]; MOVSEL_4 = INPUT[4]; MOVSEL_5 = INPUT[5]; MOVSEL_6 = INPUT[6]; MOVSEL_7 = INPUT[7];
  //   MOVSEL_8 = INPUT[8]; MOVSEL_RST = RESET
endmodule

module BOARD_MEM_1 (
  input  RESET,
  input  WRT,
  input  [8:0] INP,
  output [8:0] STATE
);

  wire [8:0] or_1_out;

  assign or_1_out = INP | STATE;  // OR_Gate or_1, 9 bits wide
  D_Flip_Flop d_ff_1 (.clk(WRT), .D(or_1_out[0]), .Q(STATE[0]), .reset(RESET));  // open: Qn, preset, en
  D_Flip_Flop d_ff_2 (.clk(WRT), .D(or_1_out[3]), .Q(STATE[3]), .reset(RESET));  // open: Qn, preset, en
  D_Flip_Flop d_ff_3 (.clk(WRT), .D(or_1_out[6]), .Q(STATE[6]), .reset(RESET));  // open: Qn, preset, en
  D_Flip_Flop d_ff_4 (.clk(WRT), .D(or_1_out[1]), .Q(STATE[1]), .reset(RESET));  // open: Qn, preset, en
  D_Flip_Flop d_ff_5 (.clk(WRT), .D(or_1_out[4]), .Q(STATE[4]), .reset(RESET));  // open: Qn, preset, en
  D_Flip_Flop d_ff_6 (.clk(WRT), .D(or_1_out[7]), .Q(STATE[7]), .reset(RESET));  // open: Qn, preset, en
  D_Flip_Flop d_ff_7 (.clk(WRT), .D(or_1_out[2]), .Q(STATE[2]), .reset(RESET));  // open: Qn, preset, en
  D_Flip_Flop d_ff_8 (.clk(WRT), .D(or_1_out[5]), .Q(STATE[5]), .reset(RESET));  // open: Qn, preset, en
  D_Flip_Flop d_ff_9 (.clk(WRT), .D(or_1_out[8]), .Q(STATE[8]), .reset(RESET));  // open: Qn, preset, en

  // Other names for the same wires on the sheet: M1R = RESET; M1W = WRT
endmodule

module COL_DET (
  input  [8:0] STATE,
  input  [8:0] MOV,
  output OK
);

  wire and_1_out, and_2_out, and_3_out, and_4_out, and_5_out, and_6_out, and_7_out, and_8_out, and_9_out;

  and and_1 (and_1_out, STATE[0], MOV[0]);
  and and_2 (and_2_out, STATE[3], MOV[3]);
  and and_3 (and_3_out, STATE[6], MOV[6]);
  and and_4 (and_4_out, STATE[1], MOV[1]);
  and and_5 (and_5_out, STATE[4], MOV[4]);
  and and_6 (and_6_out, STATE[7], MOV[7]);
  and and_7 (and_7_out, STATE[2], MOV[2]);
  and and_8 (and_8_out, STATE[5], MOV[5]);
  and and_9 (and_9_out, STATE[8], MOV[8]);
  nor nor_1 (OK, and_1_out, and_4_out, and_7_out, and_2_out, and_5_out, and_8_out, and_3_out, and_6_out, and_9_out);
endmodule

module P_MOV_OK (
  input  [8:0] B1_state,
  input  [8:0] B2_state,
  input  [8:0] pmov,
  output MOV_OK
);

  wire and_1_out, col_det_1_ok, col_det_2_ok, or_1_out;

  COL_DET col_det_1 (.STATE(B1_state), .MOV(pmov), .OK(col_det_1_ok));
  COL_DET col_det_2 (.STATE(B2_state), .MOV(pmov), .OK(col_det_2_ok));
  or or_1 (or_1_out, pmov[0], pmov[1], pmov[2], pmov[3], pmov[4], pmov[5], pmov[6], pmov[7], pmov[8]);
  and and_1 (and_1_out, col_det_1_ok, col_det_2_ok);
  and and_2 (MOV_OK, and_1_out, or_1_out);

  // Notes on the sheet:
  //   HAS MOV SELECTED
  //   IS LEGAL
endmodule

module P2_SWITCH (
  input  [8:0] PLR_MOV,
  input  [8:0] CPU_MOV,
  input  doPLR,
  output [8:0] OUT
);

  wire [8:0] and_1_out, and_2_out, not_1_out;

  assign not_1_out = ~{9{doPLR}};  // NOT_Gate not_1, 9 bits wide
  assign and_1_out = PLR_MOV & {9{doPLR}};  // AND_Gate and_1, 9 bits wide
  assign and_2_out = CPU_MOV & not_1_out;  // AND_Gate and_2, 9 bits wide
  assign OUT = and_1_out | and_2_out;  // OR_Gate or_1, 9 bits wide
endmodule

module WIN_DTCT (
  input  [8:0] STATE,
  output WIN
);

  wire and_1_out, and_2_out, and_3_out, and_4_out, and_5_out, and_6_out, and_7_out, and_8_out;

  and and_1 (and_1_out, STATE[1], STATE[0], STATE[2]);
  and and_2 (and_2_out, STATE[0], STATE[3], STATE[6]);
  and and_3 (and_3_out, STATE[0], STATE[4], STATE[8]);
  and and_4 (and_4_out, STATE[3], STATE[4], STATE[5]);
  and and_5 (and_5_out, STATE[1], STATE[4], STATE[7]);
  and and_6 (and_6_out, STATE[6], STATE[7], STATE[8]);
  and and_7 (and_7_out, STATE[2], STATE[4], STATE[6]);
  and and_8 (and_8_out, STATE[2], STATE[5], STATE[8]);
  or or_1 (WIN, and_1_out, and_4_out, and_6_out, and_2_out, and_5_out, and_8_out, and_3_out, and_7_out);

  // Other names for the same wires on the sheet: B0 = STATE[0]; B1 = STATE[1]; B2 = STATE[2]; B3 = STATE[3];
  //   B4 = STATE[4]; B5 = STATE[5]; B6 = STATE[6]; B7 = STATE[7]; B8 = STATE[8]
endmodule

module END_DTCT (
  input  [8:0] P1,
  input  [8:0] P2,
  output P1_WIN,
  output P2_WIN,
  output DRAW,
  output GAME_OVER
);

  WIN_DTCT win_dtct_1 (.STATE(P1), .WIN(P1_WIN));
  WIN_DTCT win_dtct_2 (.STATE(P2), .WIN(P2_WIN));
  DRAW_DTCT draw_dtct_1 (.P1(P1), .P2(P2), .DRAW(DRAW));
  or or_1 (GAME_OVER, P1_WIN, P2_WIN, DRAW);
endmodule

module DRAW_DTCT (
  input  [8:0] P1,
  input  [8:0] P2,
  output DRAW
);

  wire [8:0] or_1_out;

  assign or_1_out = P1 | P2;  // OR_Gate or_1, 9 bits wide
  and and_1 (DRAW, or_1_out[0], or_1_out[1], or_1_out[2], or_1_out[3], or_1_out[4], or_1_out[5], or_1_out[6], or_1_out[7], or_1_out[8]);
endmodule

module STATE_MACHINE (
  input  RESET,
  input  P1,
  input  P2,
  input  CPU,
  input  MOV_OK,
  output P2_SWTCH,
  output P1_WRT,
  output P2_WRT,
  output P1_TURN,
  output P2_TURN,
  output START_TURN
);

  wire clock_1_out;
  wire [1:0] sm_input_decode_1_input_code;
  wire [2:0] rom_1_data;
  wire [4:2] d_ff_1_q;

  SM_INPUT_DECODE sm_input_decode_1 (
    .P1(P1), .P2(P2), .CPU(CPU), .MOV_OK(MOV_OK), .INPUT_CODE(sm_input_decode_1_input_code));
  ROM #(.addrWidth(5), .dataWidth(3)) rom_1 (
    .addr({d_ff_1_q, sm_input_decode_1_input_code}), .data(rom_1_data));  // open: sel
  Clock clock_1 (.out(clock_1_out));
  D_Flip_Flop d_ff_1 (.clk(clock_1_out), .D(rom_1_data[0]), .Q(d_ff_1_q[2]), .reset(RESET));  // open: Qn, preset, en
  D_Flip_Flop d_ff_2 (.clk(clock_1_out), .D(rom_1_data[1]), .Q(d_ff_1_q[3]), .reset(RESET));  // open: Qn, preset, en
  D_Flip_Flop d_ff_3 (.clk(clock_1_out), .D(rom_1_data[2]), .Q(d_ff_1_q[4]), .reset(RESET));  // open: Qn, preset, en
  SM_OUTPUT_DECODE sm_output_decode_1 (
    .StateCode(d_ff_1_q), .START_TURN(START_TURN), .P1_TURN(P1_TURN), .P2_TURN(P2_TURN), .P1_WRT(P1_WRT),
    .P2_WRT(P2_WRT), .P2_SWTCH(P2_SWTCH));

  // Notes on the sheet:
  //   contents of rom_1 (hex, n*v repeats v):
  //   0 2 4 6 1 2 1 1 6*3 4 6 4*5 4*1 4*7 4*1
endmodule

module CPU (
  input  [8:0] P1,
  input  [8:0] P2,
  output [8:0] CPU
);

  wire [7:0] rom_1_data;

  ROM #(.addrWidth(18)) rom_1 (.addr({P2, P1}), .data(rom_1_data));  // open: sel
  ROM #(.dataWidth(9)) rom_2 (.addr(rom_1_data), .data(CPU));  // open: sel

  // Notes on the sheet:
  //   contents of rom_1 (hex, n*v repeats v):
  //   4 4 4 2 4 1 0 f 4 6 4 2 4 1 0 f 8 8 7 2 6 1 0 f 5 5 5 2 5 1 0 f 4 4 4 2 8 1 0 f 4 4 4 2 4 1 0 f 3 3
  //   3 2 3 1 0 9*f 4 3 4 2 4 1 0 f 0 f 0 f 0 f 0 f 2 3 7 2 4*f 5 f 5 5*f 4 3 4 2 8 1 0 f 4 f 4 f 4 f 0 f
  //   3 3 3 2 12*f 4 4 4 2 4 1 0 f 4 6 4 2 4 1 0 f 1 1 f f 1 1 f f 5 5 f f 5 1 f f 4 4 4 2 8 1 0 f 4 4 4 2
  //   4 1 0 f 3 3 f f 3 1 10*f 8 8 8 2 8 1 0 f 8 f 8 f 8 f 0 f 8 8 6*f 5 7*f 8 8 8 2 8 1 0 f 4 f 4 f 4 f f
  //   f 3 3 14*f 4 4 4 2 5 1 0 f 4 6 4 2 5 1 0 f 0 f 7 f 5 f 0 f 5 f 5 f 5 f 0 f 4*2 4*f 4 4 4 2 4*f 3 f 3
  //   13*f 7 7 7 2 7 1 0 f 7 f 7 f 7 f 0 f 7 f 7 5*f 5 f 5 5*f 7 7 7 2 4*f 4 f 4 5*f 3 f 3 13*f 6 6 6 2 6
  //   1 0 f 6 6 6 2 6 1 0 f 6 f f f 6 f f f 5 f f f 5 f f f 6 6 6 2 4*f 4 4 4 5*f 3 79*f 4 f 4 f 4 f 4 f 4
  //   f 4 f 4 f 4 f 6 f 7 f 6 f 7 f 5 f 5 f 5 f 5 f 4 f 4 f 8 f 8 f 4 f 4 f 4 f 4 f 3 f 3 f 3 f 3 9*f 4 f
  //   4 f 4 f 4 f 4 f 4 f 4 f 4 f 2 f 7 5*f 5 f 5 5*f 4 f 4 f 8 f 8 f 4 f 4 f 4 f 4 f 3 f 3 13*f 4 f 4 f 4
  //   f 4 f 4 f 4 f 4 f 4 f 1 f f f 1 f f f 5 f f f 5 f f f 4 f 4 f 8 f 4 f 4 f 4 f 4 f 4 f 3 f f f 3 11*f
  //   8 f 8 f 8 f 8 f 8 f 8 f 8 f 8 f 8 7*f 5 7*f 8 f 8 f 8 f 8 f 4 f 4 f 4 f 4 f 3 15*f 4 f 4 f 5 f 5 f 4
  //   f 4 f 5 f 5 f 0 f 7 f 5 f 7 f 5 f 5 f 5 f 5 f 2 f 2 5*f 4 f 4 5*f 3 f 3 13*f 7 f 7 f 7 f 7 f 7 f 7 f
  //   7 f 7 f 7 f 7 5*f 5 f 5 5*f 7 f 7 5*f 4 f 4 5*f 3 f 3 13*f 6 f 6 f 6 f 6 f 6 f 6 f 6 f 6 f 6 f f f 6
  //   f f f 5 f f f 5 f f f 6 f 6 5*f 4 f 4 5*f 3 79*f 4 4 f f 4 4 f f 4 6 f f 4 6 f f 6 8 f f 6 8 f f 5 5
  //   f f 5 5 f f 4 4 f f 8 8 f f 4 4 f f 4 4 f f 3 3 f f 3 3 10*f 4 3 f f 4 3 f f 0 f f f 0 f f f 2 3 6*f
  //   5 7*f 4 3 f f 8 3 f f 4 f f f 4 f f f 3 3 14*f 4 4 f f 4 4 f f 4 6 f f 4 6 f f 2 8 f f 6 8 f f 5 5 f
  //   f 5 5 f f 4 4 f f 8 8 f f 4 4 f f 4 4 f f 3 3 f f 3 3 10*f 8 8 f f 8 8 f f 8 f f f 8 f f f 8 8 6*f 5
  //   7*f 8 8 f f 8 8 f f 4 f f f 4 f f f 3 3 14*f 4 4 f f 5 5 f f 4 6 f f 5 6 f f 0 f f f 5 f f f 5 f f f
  //   5 f f f 2 2 6*f 4 4 6*f 3 15*f 7 7 f f 7 7 f f 7 f f f 7 f f f 7 7*f 5 7*f 7 7 6*f 4 7*f 3 15*f 6 6
  //   f f 6 6 f f 6 6 f f 6 6 f f 6 f f f 6 f f f 5 f f f 5 f f f 6 6 6*f 4 4 6*f 3 79*f 2 f f f 4 f f f 2
  //   f f f 4 f f f 2 f f f 6 f f f 2 f f f 5 f f f 2 f f f 8 f f f 2 f f f 4 f f f 2 f f f 3 11*f 2 f f f
  //   4 f f f 2 f f f 4 f f f 2 7*f 2 7*f 2 f f f 8 f f f 2 f f f 4 f f f 2 15*f 2 f f f 4 f f f 2 f f f 4
  //   f f f 2 f f f 6 f f f 2 f f f 5 f f f 2 f f f 8 f f f 2 f f f 4 f f f 2 f f f 3 11*f 2 f f f 8 f f f
  //   2 f f f 8 f f f 2 7*f 2 7*f 2 f f f 8 f f f 2 f f f 4 f f f 2 15*f 2 f f f 5 f f f 2 f f f 5 f f f 2
  //   f f f 5 f f f 2 f f f 5 f f f 2 7*f 2 7*f 2 15*f 2 f f f 7 f f f 2 f f f 7 f f f 2 7*f 2 7*f 2 7*f 2
  //   7*f 2 15*f 2 f f f 6 f f f 2 f f f 6 f f f 2 f f f 6 f f f 2 f f f 5 f f f 2 7*f 2 7*f 2 79*f 4*4
  //   4*f 4 6 4 6 4*f 0 8 7 7 4*f 4*5 4*f 4*4 4*f 4*4 4*f 4*3 12*f 4 3 4 3 4*f 0 f 0 5*f 0 3 7 3 4*f 5 f 5
  //   5*f 4 3 4 3 4*f 4 f 4 5*f 4*3 12*f 4*4 4*f 4 6 4 6 4*f 1 1 6*f 5 5 6*f 4*4 4*f 4*4 4*f 3 3 14*f 4*8
  //   4*f 8 f 8 5*f 8 8 6*f 5 7*f 4*8 4*f 4 f 4 5*f 3 3 14*f 4*4 4*f 4 6 4 6 4*f 0 f 7 5*f 5 f 5 5*f 4*4
  //   4*f 4*4 4*f 3 f 3 13*f 4*7 4*f 7 f 7 5*f 7 f 7 5*f 5 f 5 5*f 4*7 4*f 4 f 4 5*f 3 f 3 13*f 4*6 4*f
  //   4*6 4*f 6 7*f 5 7*f 4*6 4*f 4*4 4*f 3 79*f 1 f 4 5*f 1 f 4 5*f 1 f 7 5*f 1 f 5 5*f 1 f 4 5*f 1 f 4
  //   5*f 1 f 3 13*f 1 f 4 5*f 1 f 4 5*f 1 f 7 5*f 1 f 5 5*f 1 f 4 5*f 1 f 4 5*f 1 f 3 13*f 1 f 4 5*f 1 f
  //   4 5*f 1 7*f 1 7*f 1 f 4 5*f 1 f 4 5*f 1 15*f 1 f 8 5*f 1 f 8 5*f 1 7*f 1 7*f 1 f 8 5*f 1 f 4 5*f 1
  //   15*f 1 f 4 5*f 1 f 4 5*f 1 f 7 5*f 1 f 5 5*f 1 f 4 5*f 1 f 4 5*f 1 f 3 13*f 1 f 7 5*f 1 f 7 5*f 1 f
  //   7 5*f 1 f 5 5*f 1 f 7 5*f 1 f 4 5*f 1 f 3 13*f 1 f 6 5*f 1 f 6 5*f 1 7*f 1 7*f 1 f 6 5*f 1 f 4 5*f 1
  //   79*f 0 4 6*f 0 6 6*f 0 8 6*f 0 5 6*f 0 4 6*f 0 4 6*f 0 3 14*f 0 3 6*f 0 7*f 0 3 6*f 0 7*f 0 3 6*f 0
  //   7*f 0 3 14*f 0 4 6*f 0 6 6*f 0 8 6*f 0 5 6*f 0 4 6*f 0 4 6*f 0 3 14*f 0 8 6*f 0 7*f 0 8 6*f 0 7*f 0
  //   8 6*f 0 7*f 0 3 14*f 0 4 6*f 0 6 6*f 0 7*f 0 7*f 0 4 6*f 0 4 6*f 0 15*f 0 7 6*f 0 7*f 0 7*f 0 7*f 0
  //   7 6*f 0 7*f 0 15*f 0 6 6*f 0 6 6*f 0 7*f 0 7*f 0 6 6*f 0 4 6*f 0 591*f 4 4 4 2 4 1 0 9*f 0 8 7 2 6 1
  //   0 9*f 4 4 4 2 8 1 0 9*f 0 8 7 2 8 1 0 9*f 4 4 4 2 4 1 0 9*f 2 8 7 2 12*f 4 4 4 2 8 1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
  //   contents of rom_2 (hex, n*v repeats v):
  //   1 2 4 8 10 20 40 80 100
endmodule

module SM_INPUT_DECODE (
  input  P1,
  input  P2,
  input  CPU,
  input  MOV_OK,
  output [1:0] INPUT_CODE
);

  wire and_1_out, and_2_out;

  and and_1 (and_1_out, P1, MOV_OK);
  and and_2 (and_2_out, P2, MOV_OK);
  or or_1 (INPUT_CODE[0], and_1_out, CPU);
  or or_2 (INPUT_CODE[1], and_2_out, CPU);
endmodule

module SM_OUTPUT_DECODE (
  input  [2:0] StateCode,
  output START_TURN,
  output P1_TURN,
  output P2_TURN,
  output P1_WRT,
  output P2_WRT,
  output P2_SWTCH
);

  wire not_1_out, not_2_out, not_3_out, not_4_out, not_5_out;

  nor nor_1 (START_TURN, StateCode[0], StateCode[1], StateCode[2]);
  not not_1 (not_1_out, StateCode[0]);
  nor nor_2 (P1_TURN, not_1_out, StateCode[1], StateCode[2]);
  not not_2 (not_2_out, StateCode[0]);
  not not_3 (not_3_out, StateCode[1]);
  nor nor_3 (P2_TURN, not_2_out, not_3_out, StateCode[2]);
  nor nor_4 (P1_WRT, StateCode[0], not_4_out, StateCode[2]);
  not not_4 (not_4_out, StateCode[1]);
  and and_1 (P2_WRT, StateCode[0], StateCode[2]);
  and and_2 (P2_SWTCH, StateCode[2], not_5_out);
  not not_5 (not_5_out, StateCode[1]);
endmodule

module SM_TRANSITION (
  input  [1:0] INPUT,
  input  [2:0] NEW_STATE,
  input  [2:0] STATE
);
endmodule

module SM_TR_Q0 (
  input  [1:0] INPUT,
  input  [2:0] STATE,
  output out_3
);

  // NOT_Gate not_1 is placed but not wired
  // NOT_Gate not_2 is placed but not wired
  // NOT_Gate not_3 is placed but not wired
  // NOT_Gate not_4 is placed but not wired
  // NOT_Gate not_5 is placed but not wired
endmodule
